// Digital circuit SuperController.dig as structural Verilog
module SuperController (
  input  BEGIN,
  input  CLK,
  input  PHASE_END,
  output [1:0] PHASE,
  output PHASE_BEGIN,
  output END
);

  wire d_ff_1_q, or_1_out, xor_1_out;
  wire [1:0] counter_1_out;

  xor xor_1 (xor_1_out, PHASE_END, BEGIN);
  or or_1 (or_1_out, BEGIN, PHASE_END);
  Counter #(.Bits(2)) counter_1 (.en(1'b1), .C(xor_1_out), .clr(BEGIN), .out(counter_1_out));  // open: ovf
  D_FF d_ff_1 (.D(or_1_out), .C(CLK), .Q(d_ff_1_q));  // open: nQ
  Add #(.Bits(2)) add_1 (.a(counter_1_out), .b(2'b01), .c_i(1'b0), .s(PHASE));  // open: c_o
  and and_1 (END, counter_1_out[0], counter_1_out[1]);
  and and_2 (PHASE_BEGIN, ~END, d_ff_1_q);  // And
endmodule
