// Digital circuit Corrector.dig as structural Verilog
module Corrector (
  input  [3:0] SUM,
  input  [3:0] SEL,
  output [3:0] OUT
);

  wire and_1_out, not_2_out, or_1_out, or_2_out, or_3_out, or_4_out, or_5_out, xor_1_out, xor_2_out;
  wire [3:1] not_1_out;

  not not_1 (not_1_out[1], SUM[1]);
  not not_2 (not_2_out, SUM[2]);
  xor xor_1 (xor_1_out, SUM[1], SEL[0]);
  xor xor_2 (xor_2_out, SEL[0], SUM[2]);
  or or_1 (or_1_out, SUM[2], SUM[3]);
  xor xor_3 (not_1_out[2], not_2_out, xor_1_out);
  or or_2 (or_2_out, ~SUM[2], ~SUM[3]);  // Or
  xor xor_4 (not_1_out[3], SUM[3], or_4_out);
  or or_3 (or_3_out, SUM[0], SUM[1], SUM[3]);
  or or_4 (or_4_out, xor_1_out, xor_2_out);
  or or_5 (or_5_out, ~SUM[0], ~SUM[1], ~SUM[3]);  // Or
  and and_1 (and_1_out, or_5_out, or_3_out, or_2_out, or_1_out);
  Multiplexer #(.Bits(4)) multiplexer_1 (.sel(and_1_out), .in_0(SUM), .in_1({not_1_out, SUM[0]}), .out(OUT));
  // Pins of 1 and 4 bits meet at SEL

  // Other names for the same wires on the sheet: C_T1[3:0] = SEL
endmodule
