// Digital circuit CorrectorD.dig as structural Verilog
module CorrectorD (
  input  [3:0] SUM,
  input  [3:0] SEL,
  output [3:0] OUT
);

  wire andd_1_p5, notd_2_p2, notd_4_p2, notd_5_p2, notd_6_p2, notd_7_p2, ord_1_p2, ord_2_p2, ord_2_p4,
       ord_5_p2, xord_1_p3, xord_2_p3, xord_3_p1, xord_4_p3;
  wire [3:1] notd_1_p2;

  // NotD #(.generic("inputCount := 1 ;")) notd_1: pin names not known; wires that end beside it: SUM[1], notd_1_p2[1]
  // NotD #(.generic("inputCount := 1;")) notd_2: pin names not known; wires that end beside it: SUM[3], notd_2_p2
  // OrD #(.generic("inputCount := 2;")) ord_1: pin names not known; wires that end beside it: SUM[3], ord_1_p2, SUM[2]
  // NotD #(.generic("inputCount := 1 ;")) notd_3: pin names not known; wires that end beside it: SUM[2]
  // XorD #(.generic("inputCount := 2;")) xord_1: pin names not known; wires that end beside it: SUM[1], SEL, xord_1_p3
  // XorD #(.generic("inputCount := 2;")) xord_2: pin names not known; wires that end beside it: SEL, SUM[2], xord_2_p3
  // NotD #(.generic("inputCount := 1;")) notd_4: pin names not known; wires that end beside it: SUM[2], notd_4_p2
  // OrD #(.generic("inputCount := 2;")) ord_2: pin names not known; wires that end beside it: notd_2_p2, ord_2_p2, notd_4_p2, ord_2_p4
  // XorD #(.generic("inputCount := 2;")) xord_3: pin names not known; wires that end beside it: xord_3_p1, xord_3_p1, notd_1_p2[2], xord_1_p3
  // NotD #(.generic("inputCount := 1;")) notd_5: pin names not known; wires that end beside it: SUM[3], notd_5_p2
  // OrD #(.generic("inputCount := 3;")) ord_3: pin names not known; wires that end beside it: SUM[3], SUM[1], SUM[0], notd_5_p2
  // XorD #(.generic("inputCount := 2;")) xord_4: pin names not known; wires that end beside it: SUM[3], notd_1_p2[3], xord_4_p3
  // OrD #(.generic("inputCount := 2;")) ord_4: pin names not known; wires that end beside it: xord_1_p3, xord_2_p3, xord_4_p3
  // NotD #(.generic("inputCount := 1;")) notd_6: pin names not known; wires that end beside it: SUM[1], notd_6_p2
  // NotD #(.generic("inputCount := 1;")) notd_7: pin names not known; wires that end beside it: SUM[0], notd_7_p2, SUM[0], SUM[1], SUM[2], SUM[3]
  // OrD #(.generic("inputCount := 3;")) ord_5: pin names not known; wires that end beside it: notd_6_p2, ord_5_p2, notd_7_p2
  // AndD #(.generic("inputCount := 4;")) andd_1: pin names not known; wires that end beside it: ord_5_p2, ord_2_p4, ord_2_p2, ord_1_p2, andd_1_p5
  Multiplexer #(.Bits(4)) multiplexer_1 (.sel(andd_1_p5), .in_0(SUM), .in_1({notd_1_p2, SUM[0]}), .out(OUT));

  // Other names for the same wires on the sheet: C_T1[3:0] = SEL
endmodule
