// Digital circuit NandD.dig as structural Verilog
module NandD (
  output Q
);

  wire nand_1_out, undriven, undriven_2, undriven_3, undriven_4;

  nand nand_1 (nand_1_out, undriven, undriven_2, undriven_3, undriven_4, 1'b1, 1'b1, 1'b1, 1'b1, 1'b1);
  Delay #(.generic("initD := 1; riseD := 1; this.delayTime = initD + (riseD * args.inputCount);")) delay_1 (
    .in(nand_1_out), .out(Q));
endmodule

/* Code that sets the parameters or builds the circuit:
inputCount := 6;
*/

/* Code that sets the parameters or builds the circuit:
for (i:=0; i <args.inputCount; i++) {
 inp:=addComponent("In",0,i);
 inp.Label="D" + i;
}
*/
