// Digital circuit NotD.dig as structural Verilog
module NotD (
  input  [5:0] D,
  output Q
);

  wire [5:0] not_1_out;

  Delay #(.generic("initD := 1; riseD := 1; this.delayTime = initD + (riseD * args.inputCount); this.Bits = args.inputCount;")) delay_1 (
    .in(not_1_out), .out(Q));
  assign not_1_out = ~D;  // Not not_1, 6 bits wide
  // Pins of 4 and 6 bits meet at D
endmodule

/* Code that sets the parameters or builds the circuit:
inputCount := 6;
*/
